# Fritzing sketch WS2812_ATmega328p (saved by Fritzing 0.9.10b)
breadboards: 1

parts:
  R1 = Resistor [tolerance=±5% power=0.25 resistance=10k package=THT]
  U1 = atmega328 [package=dip]
  Y1 = CRYSTAL [package=hc49us]
  C1 = Capacitor [package=cap-pth-small2]
  C2 = Capacitor [package=cap-pth-small2]
  U2 = WS2812 RGB LED matrix 1x8

nets:
  N1: R1.Pin_0, U1.RESET
  VCC: R1.Pin_1, U1.VCC, U2.VCC
  N2: U1.GND#7, C1.1, C2.2, U2.GND
  N3: U1.XLAT1, Y1.1, C1.2
  N4: U1.XLAT2, Y1.2, C2.1
  N5: U1.D9_(PWM), U2.DIN

custom parts:
  WS2812 RGB LED matrix 1x8: WS2812 matrix 1x8
